// Logisim project Trabalho Final.circ as structural Verilog: 3 circuits, main circuit main
module main (
);

  Clock clock_1 ();  // open: out
  Contador_0_7 contador_0_7_1 ();  // open: E, S
  Acumulador acumulador_1 ();  // open: Entrada, WE, Saída
endmodule

module Contador_0_7 (
  input  E,
  output S
);

  wire t_ff_1_q, t_ff_2_q;

  T_Flip_Flop #(.trigger("falling")) t_ff_1 (.clk(E), .T(1'b1), .Q(t_ff_1_q));  // open: Qn, preset, reset, en
  T_Flip_Flop #(.trigger("falling")) t_ff_2 (.clk(t_ff_1_q), .T(1'b1), .Q(t_ff_2_q));  // open: Qn, preset, reset, en
  T_Flip_Flop #(.trigger("falling")) t_ff_3 (.clk(t_ff_2_q), .T(1'b1), .Q(S));  // open: Qn, preset, reset, en
endmodule

module Acumulador (
  input  [10:0] Entrada,
  input  WE,
  output [10:0] \Saída 
);

  D_Flip_Flop d_ff_1 (.clk(WE), .D(Entrada[0]), .Q(\Saída [0]));  // open: Qn, preset, en, reset
  D_Flip_Flop d_ff_2 (.clk(WE), .D(Entrada[1]), .Q(\Saída [1]));  // open: Qn, preset, en, reset
  D_Flip_Flop d_ff_3 (.clk(WE), .D(Entrada[2]), .Q(\Saída [2]));  // open: Qn, preset, en, reset
  D_Flip_Flop d_ff_4 (.clk(WE), .D(Entrada[3]), .Q(\Saída [3]));  // open: Qn, preset, en, reset
  D_Flip_Flop d_ff_5 (.clk(WE), .D(Entrada[4]), .Q(\Saída [4]));  // open: Qn, preset, en, reset
  D_Flip_Flop d_ff_6 (.clk(WE), .D(Entrada[5]), .Q(\Saída [5]));  // open: Qn, preset, en, reset
  D_Flip_Flop d_ff_7 (.clk(WE), .D(Entrada[6]), .Q(\Saída [6]));  // open: Qn, preset, en, reset
  D_Flip_Flop d_ff_8 (.clk(WE), .D(Entrada[7]), .Q(\Saída [7]));  // open: Qn, preset, en, reset
  D_Flip_Flop d_ff_9 (.clk(WE), .D(Entrada[8]), .Q(\Saída [8]));  // open: Qn, preset, en, reset
  D_Flip_Flop d_ff_10 (.clk(WE), .D(Entrada[9]), .Q(\Saída [9]));  // open: Qn, preset, en, reset
  D_Flip_Flop d_ff_11 (.clk(WE), .D(Entrada[10]), .Q(\Saída [10]));  // open: Qn, preset, en, reset
endmodule
